// Logisim project De morgan's Theorems1.circ as structural Verilog: 1 circuit, main circuit main
module main (
  input  A,
  input  A_2,
  input  B,
  input  B_2,
  input  A_3,
  input  A_4,
  input  B_3,
  input  B_4,
  output NOT_A_B,
  output out_10,
  output NOT_AB,
  output out_12
);

  wire AND_out, NOT_3_out, NOT_4_out, NOT_5_out, NOT_6_out, OR_out;

  and AND (AND_out, A_3, B_4);
  or OR (OR_out, A, B_2);
  not NOT (NOT_AB, AND_out);
  not NOT_2 (NOT_A_B, OR_out);
  not NOT_3 (NOT_3_out, A_2);
  not NOT_4 (NOT_4_out, B);
  not NOT_5 (NOT_5_out, A_4);
  not NOT_6 (NOT_6_out, B_3);
  and AND_2 (out_10, NOT_3_out, NOT_4_out);
  or OR_2 (out_12, NOT_5_out, NOT_6_out);
endmodule
