// Logisim project universal gates 2.circ as structural Verilog: 1 circuit, main circuit main
module main (
  input  A,
  input  A_2,
  input  B,
  input  A_3,
  input  B_2,
  output Not_A,
  output A_B,
  output A_B_2
);

  wire NOR_2_out, NOR_3_out, NOR_out;

  nor NOR (NOR_out, A_2, B);
  nor NOR_2 (NOR_2_out, A_3, A_3);
  nor NOR_3 (NOR_3_out, B_2, B_2);
  nor NOR_4 (Not_A, A, A);
  nor NOR_5 (A_B, NOR_out, NOR_out);
  nor NOR_6 (A_B_2, NOR_2_out, NOR_3_out);
endmodule
